// Logisim project ChaCha20.circ as structural Verilog: 5 circuits, main circuit main
module main (
  input  in_1,
  input  LOCK,
  input  COUNTER_INITIAL,
  input  in_4,
  input  in_5,
  input  in_6,
  input  _8_BIT_KEY,
  input  in_8,
  input  in_9,
  input  in_10,
  input  in_11,
  input  in_12,
  input  NONCE,
  input  in_14,
  input  in_15,
  input  _0,
  input  _1,
  output out_18
);

  wire counter_1_lsb, counter_1_msb, key_stream_generator_1_k0, not_1_out, plain_text_input_1_bit_value,
       plain_text_input_1_flag;

  Plain_Text_Input plain_text_input_1 (
    .input_1(_0), .input_0(_1), .flag(plain_text_input_1_flag), .Bit_Value(plain_text_input_1_bit_value));
  Counter counter_1 (
    .in_1(plain_text_input_1_flag), .INIT_LSB(in_4), .INIT_MSB(COUNTER_INITIAL), .Lock(LOCK),
    .MSB(counter_1_msb), .LSB(counter_1_lsb));
  not not_1 (not_1_out, in_15);
  Key_Stream_Generator key_stream_generator_1 (
    .x(in_15), .x_2(not_1_out), .x_3(not_1_out), .x_4(in_15), .in_5(in_5), .in_6(in_6), .Key(_8_BIT_KEY),
    .in_8(in_8), .in_9(in_9), .in_10(in_10), .in_11(in_11), .in_12(in_12), .MSB(counter_1_msb),
    .LSB(counter_1_lsb), .Nonce(NONCE), .in_16(in_14), .K0(key_stream_generator_1_k0));
  xor xor_1 (out_18, plain_text_input_1_bit_value, key_stream_generator_1_k0);
endmodule

// COUNT
module Counter (
  input  in_1,
  input  INIT_LSB,
  input  INIT_MSB,
  input  Lock,
  output MSB,
  output LSB
);

  wire And1_out, And2_out, And3_out, And4_out, d_ff_1_qn, d_ff_2_qn, not_1_out, not_2_out, not_3_out;

  and And1 (And1_out, INIT_LSB, Lock);
  D_Flip_Flop d_ff_1 (
    .clk(in_1), .D(d_ff_1_qn), .Q(LSB), .Qn(d_ff_1_qn), .preset(And1_out), .reset(And2_out));  // open: en
  and And2 (And2_out, not_1_out, Lock);
  not not_1 (not_1_out, INIT_LSB);
  not not_2 (not_2_out, LSB);
  D_Flip_Flop d_ff_2 (
    .clk(not_2_out), .D(d_ff_2_qn), .Q(MSB), .Qn(d_ff_2_qn), .preset(And3_out), .reset(And4_out));  // open: en
  and And3 (And3_out, INIT_MSB, Lock);
  and And4 (And4_out, not_3_out, Lock);
  not not_3 (not_3_out, INIT_MSB);

  // Notes on the sheet:
  //   COUNTER
endmodule

// QRG
module Quarter_Round_Generator (
  input  A,
  input  B,
  input  C,
  input  D,
  output a_2,
  output b_2,
  output c_2,
  output d_2
);

  wire adder_1_out, adder_3_out, Xor1_out, Xor2_out;

  Adder #(.width(1)) adder_1 (.a(B), .b(A), .out(adder_1_out));  // open: cin, cout
  xor Xor2 (Xor2_out, B, adder_3_out);
  xor Xor4 (b_2, Xor2_out, c_2);
  Adder #(.width(1)) adder_2 (.a(Xor2_out), .b(adder_1_out), .out(a_2));  // open: cin, cout
  xor Xor1 (Xor1_out, adder_1_out, D);
  xor Xor3 (d_2, a_2, Xor1_out);
  Adder #(.width(1)) adder_3 (.a(Xor1_out), .b(C), .out(adder_3_out));  // open: cin, cout
  Adder #(.width(1)) adder_4 (.a(adder_3_out), .b(d_2), .out(c_2));  // open: cin, cout

  // Notes on the sheet:
  //   Add1
  //   Add3
  //   QUARTER ROUND GENERATOR
  //   Add2
  //   Add4
endmodule

// KSG
module Key_Stream_Generator (
  input  x,
  input  x_2,
  input  x_3,
  input  x_4,
  input  in_5,
  input  in_6,
  input  Key,
  input  in_8,
  input  in_9,
  input  in_10,
  input  in_11,
  input  in_12,
  input  MSB,
  input  LSB,
  input  Nonce,
  input  in_16,
  output K0
);

  wire quarter_round_generator_1_a_2, quarter_round_generator_2_b_2, quarter_round_generator_3_a_2,
       quarter_round_generator_4_c_2, quarter_round_generator_5_d_2;

  Quarter_Round_Generator quarter_round_generator_1 (
    .A(x), .B(in_5), .C(in_6), .D(MSB), .a_2(quarter_round_generator_1_a_2));  // open: b_2, c_2, d_2
  Quarter_Round_Generator quarter_round_generator_2 (
    .A(x_2), .B(Key), .C(in_8), .D(LSB), .b_2(quarter_round_generator_2_b_2));  // open: a_2, c_2, d_2
  Quarter_Round_Generator quarter_round_generator_3 (
    .A(quarter_round_generator_1_a_2), .B(quarter_round_generator_2_b_2), .C(quarter_round_generator_4_c_2),
    .D(quarter_round_generator_5_d_2), .a_2(quarter_round_generator_3_a_2));  // open: b_2, c_2, d_2
  Quarter_Round_Generator quarter_round_generator_4 (
    .A(x_3), .B(in_9), .C(in_10), .D(Nonce), .c_2(quarter_round_generator_4_c_2));  // open: a_2, b_2, d_2
  Adder #(.width(1)) adder_1 (.a(quarter_round_generator_3_a_2), .b(x), .out(K0));  // open: cin, cout
  Quarter_Round_Generator quarter_round_generator_5 (
    .A(x_4), .B(in_11), .C(in_12), .D(in_16), .d_2(quarter_round_generator_5_d_2));  // open: a_2, b_2, c_2

  // Notes on the sheet:
  //   KEY STREAM GENERATOR
  //   Counter
endmodule

module Plain_Text_Input (
  input  input_1,
  input  input_0,
  output flag,
  output Bit_Value
);

  or or_1 (flag, input_1, input_0);

  assign Bit_Value = input_1;

  // Notes on the sheet:
  //   PLAIN TEXT INPUT
endmodule
